// Logisim project CRC.circ as structural Verilog: 2 circuits, main circuit CRC
module CRC (
  input  [7:0] A,
  input  [3:0] B,
  output [10:0] C
);

  wire [3:1] intialize1, intialize2, intialize3, intialize4, intialize5, intialize6, intialize7;
  wire [10:0] divisor, extend_A;

  assign extend_A = {{3{1'b0}}, A};  // Bit_Extender bit_extender_1
  Shifter #(.width(11)) shifter_1 (.in(extend_A), .\dist (4'b0011), .out(divisor));
  _4bit_mod2_divide u_4bit_mod2_divide_1 (.divisor(divisor[10:7]), .divider(B), .mod(intialize1));
  _4bit_mod2_divide u_4bit_mod2_divide_2 (.divisor({intialize1, divisor[6]}), .divider(B), .mod(intialize2));
  _4bit_mod2_divide u_4bit_mod2_divide_3 (.divisor({intialize2, divisor[5]}), .divider(B), .mod(intialize3));
  _4bit_mod2_divide u_4bit_mod2_divide_4 (.divisor({intialize3, divisor[4]}), .divider(B), .mod(intialize4));
  _4bit_mod2_divide u_4bit_mod2_divide_5 (.divisor({intialize4, divisor[3]}), .divider(B), .mod(intialize5));
  _4bit_mod2_divide u_4bit_mod2_divide_6 (.divisor({intialize5, divisor[2]}), .divider(B), .mod(intialize6));
  _4bit_mod2_divide u_4bit_mod2_divide_7 (.divisor({intialize6, divisor[1]}), .divider(B), .mod(intialize7));
  _4bit_mod2_divide u_4bit_mod2_divide_8 (.divisor({intialize7, divisor[0]}), .divider(B), .mod(C[2:0]));

  assign C[10:3] = A;

  // Other names for the same wires on the sheet: process7[2:0] = C[2:0]; divider[3:0] = B;
  //   initialize0[3:0] = divisor[10:7]; intialize1[0] = divisor[6]; process0[2:0] = intialize1;
  //   intialize2[0] = divisor[5]; process1[2:0] = intialize2; intialize3[0] = divisor[4]; process2[2:0] = intialize3;
  //   intialize4[0] = divisor[3]; process3[2:0] = intialize4; intialize5[0] = divisor[2]; process4[2:0] = intialize5;
  //   intialize6[0] = divisor[1]; process5[2:0] = intialize6; intialize7[0] = divisor[0]; process6[2:0] = intialize7
endmodule

module _4bit_mod2_divide (
  input  [3:0] divisor,
  input  [3:0] divider,
  output [2:0] mod
);

  wire [3:0] XOR_result;
  wire [3:3] out;

  assign XOR_result = divisor ^ divider;  // XOR_Gate xor_1, 4 bits wide
  Multiplexer #(.width(4)) multiplexer_1 (
    .in0(divisor), .in1(XOR_result), .out({out[3], mod}), .sel(divisor[3]));  // open: en

  // Other names for the same wires on the sheet: MSB = divisor[3]; out[2:0] = mod
endmodule
