// Logisim project GRF.circ as structural Verilog: 1 circuit, main circuit grf
module grf (
  input  clk,
  input  reset,
  input  WE,
  input  [4:0] A1,
  input  [4:0] A2,
  input  [4:0] A3,
  input  [31:0] WD,
  output [31:0] RD1,
  output [31:0] RD2
);

  wire WE1, WE2, WE3, WE4, WE5, WE6, WE7, WE8, WE9, WE10, WE11, WE12, WE13, WE14, WE15, WE16, WE17, WE18,
       WE19, WE20, WE21, WE22, WE23, WE24, WE25, WE26, WE27, WE28, WE29, WE30, WE31, WE32;
  wire [31:0] data1, data2, data3, data4, data5, data6, data7, data8, data9, data10, data11, data12, data13,
       data14, data15, data16, data17, data18, data19, data20, data21, data22, data23, data24, data25,
       data26, data27, data28, data29, data30, data31, data32;

  Register #(.width(32)) register_1 (.D(WD), .en(WE1), .Q(data1), .clk(clk), .clr(reset));
  Register #(.width(32)) register_2 (.D(WD), .en(WE2), .Q(data2), .clk(clk), .clr(reset));
  Register #(.width(32)) register_3 (.D(WD), .en(WE3), .Q(data3), .clk(clk), .clr(reset));
  Register #(.width(32)) register_4 (.D(WD), .en(WE4), .Q(data4), .clk(clk), .clr(reset));
  Register #(.width(32)) register_5 (.D(WD), .en(WE5), .Q(data5), .clk(clk), .clr(reset));
  Register #(.width(32)) register_6 (.D(WD), .en(WE6), .Q(data6), .clk(clk), .clr(reset));
  Register #(.width(32)) register_7 (.D(WD), .en(WE7), .Q(data7), .clk(clk), .clr(reset));
  Register #(.width(32)) register_8 (.D(WD), .en(WE8), .Q(data8), .clk(clk), .clr(reset));
  Register #(.width(32)) register_9 (.D(WD), .en(WE9), .Q(data9), .clk(clk), .clr(reset));
  Register #(.width(32)) register_10 (.D(WD), .en(WE10), .Q(data10), .clk(clk), .clr(reset));
  Register #(.width(32)) register_11 (.D(WD), .en(WE11), .Q(data11), .clk(clk), .clr(reset));
  Register #(.width(32)) register_12 (.D(WD), .en(WE12), .Q(data12), .clk(clk), .clr(reset));
  Register #(.width(32)) register_13 (.D(WD), .en(WE13), .Q(data13), .clk(clk), .clr(reset));
  Register #(.width(32)) register_14 (.D(WD), .en(WE14), .Q(data14), .clk(clk), .clr(reset));
  Register #(.width(32)) register_15 (.D(WD), .en(WE15), .Q(data15), .clk(clk), .clr(reset));
  Register #(.width(32)) register_16 (.D(WD), .en(WE16), .Q(data16), .clk(clk), .clr(reset));
  Register #(.width(32)) register_17 (.D(WD), .en(WE17), .Q(data17), .clk(clk), .clr(reset));
  Register #(.width(32)) register_18 (.D(WD), .en(WE18), .Q(data18), .clk(clk), .clr(reset));
  Register #(.width(32)) register_19 (.D(WD), .en(WE19), .Q(data19), .clk(clk), .clr(reset));
  Register #(.width(32)) register_20 (.D(WD), .en(WE20), .Q(data20), .clk(clk), .clr(reset));
  Register #(.width(32)) register_21 (.D(WD), .en(WE21), .Q(data21), .clk(clk), .clr(reset));
  Register #(.width(32)) register_22 (.D(WD), .en(WE22), .Q(data22), .clk(clk), .clr(reset));
  Register #(.width(32)) register_23 (.D(WD), .en(WE23), .Q(data23), .clk(clk), .clr(reset));
  Register #(.width(32)) register_24 (.D(WD), .en(WE24), .Q(data24), .clk(clk), .clr(reset));
  Register #(.width(32)) register_25 (.D(WD), .en(WE25), .Q(data25), .clk(clk), .clr(reset));
  Register #(.width(32)) register_26 (.D(WD), .en(WE26), .Q(data26), .clk(clk), .clr(reset));
  Register #(.width(32)) register_27 (.D(WD), .en(WE27), .Q(data27), .clk(clk), .clr(reset));
  Register #(.width(32)) register_28 (.D(WD), .en(WE28), .Q(data28), .clk(clk), .clr(reset));
  Register #(.width(32)) register_29 (.D(WD), .en(WE29), .Q(data29), .clk(clk), .clr(reset));
  Register #(.width(32)) register_30 (.D(WD), .en(WE30), .Q(data30), .clk(clk), .clr(reset));
  Register #(.width(32)) register_31 (.D(WD), .en(WE31), .Q(data31), .clk(clk), .clr(reset));
  Register #(.width(32)) register_32 (.D(WD), .en(WE32), .Q(data32), .clk(clk), .clr(reset));
  Decoder #(.select(5), .disabled(0)) decoder_1 (
    .out0(WE1), .out1(WE2), .out2(WE3), .out3(WE4), .out4(WE5), .out5(WE6), .out6(WE7), .out7(WE8),
    .out8(WE9), .out9(WE10), .out10(WE11), .out11(WE12), .out12(WE13), .out13(WE14), .out14(WE15),
    .out15(WE16), .out16(WE17), .out17(WE18), .out18(WE19), .out19(WE20), .out20(WE21), .out21(WE22),
    .out22(WE23), .out23(WE24), .out24(WE25), .out25(WE26), .out26(WE27), .out27(WE28), .out28(WE29),
    .out29(WE30), .out30(WE31), .out31(WE32), .sel(A3), .en(WE));
  Multiplexer #(.select(5), .width(32)) multiplexer_1 (
    .in0({32{1'b0}}), .in1(data2), .in2(data3), .in3(data4), .in4(data5), .in5(data6), .in6(data7),
    .in7(data8), .in8(data9), .in9(data10), .in10(data11), .in11(data12), .in12(data13), .in13(data14),
    .in14(data15), .in15(data16), .in16(data17), .in17(data18), .in18(data19), .in19(data20), .in20(data21),
    .in21(data22), .in22(data23), .in23(data24), .in24(data25), .in25(data26), .in26(data27), .in27(data28),
    .in28(data29), .in29(data30), .in30(data31), .in31(data32), .out(RD1), .sel(A1));  // open: en
  Multiplexer #(.select(5), .width(32)) multiplexer_2 (
    .in0({32{1'b0}}), .in1(data2), .in2(data3), .in3(data4), .in4(data5), .in5(data6), .in6(data7),
    .in7(data8), .in8(data9), .in9(data10), .in10(data11), .in11(data12), .in12(data13), .in13(data14),
    .in14(data15), .in15(data16), .in16(data17), .in17(data18), .in18(data19), .in19(data20), .in20(data21),
    .in21(data22), .in22(data23), .in23(data24), .in24(data25), .in25(data26), .in26(data27), .in27(data28),
    .in28(data29), .in29(data30), .in30(data31), .in31(data32), .out(RD2), .sel(A2));  // open: en
endmodule
