// Logisim project fsm.circ as structural Verilog: 3 circuits, main circuit fsm
module fsm (
  input  CLR,
  input  [1:0] In,
  output Z
);

  wire CLK, signal;
  wire [1:0] register_1_q, status_pass_1_status_out;

  Clock clock_1 (.out(CLK));
  status_pass status_pass_1 (.status(register_1_q), .\input (In), .status_out(status_pass_1_status_out));
  Register #(.width(2)) register_1 (
    .D(status_pass_1_status_out), .Q(register_1_q), .clk(CLK), .clr(signal));  // open: en
  Register #(.width(1)) register_2 (.D(CLR), .Q(signal), .clk(CLK), .clr(signal));  // open: en
  print print_1 (.status(register_1_q), .\input (In), .out(Z));
endmodule

module status_pass (
  input  [1:0] status,
  input  [1:0] \input ,
  output [1:0] status_out
);

  wire and_1_out, and_2_out, and_3_out, and_4_out, not_1_out, not_2_out, not_3_out, not_4_out, not_5_out,
       not_6_out, not_7_out;

  not not_1 (not_1_out, status[1]);
  not not_2 (not_2_out, \input [0]);
  not not_3 (not_3_out, status[0]);
  not not_4 (not_4_out, \input [0]);
  not not_5 (not_5_out, \input [1]);
  not not_6 (not_6_out, status[0]);
  not not_7 (not_7_out, \input [0]);
  and and_1 (and_1_out, not_1_out, status[0], not_2_out);
  and and_2 (and_2_out, status[1], not_3_out, not_4_out);
  and and_3 (and_3_out, not_5_out, \input [0]);
  and and_4 (and_4_out, status[1], not_6_out, not_7_out);
  or or_1 (status_out[1], and_1_out, and_2_out);
  or or_2 (status_out[0], and_3_out, and_4_out);
endmodule

module print (
  input  [1:0] status,
  input  [1:0] \input ,
  output out
);

  wire not_1_out, not_2_out;

  not not_1 (not_1_out, status[0]);
  not not_2 (not_2_out, \input [0]);
  and and_1 (out, status[1], not_1_out, not_2_out);
endmodule
