// Logisim project ftoi.circ as structural Verilog: 1 circuit, main circuit ftoi
module ftoi (
  input  [15:0] float,
  output [31:0] \int 
);

  wire comparator_1_eq, comparator_1_gt, select;
  wire [4:0] E, shifter;
  wire [9:0] out;
  wire [21:0] mid;
  wire [31:0] \final , operand, sign_mid;

  Multiplexer #(.width(5)) multiplexer_1 (.in0({5{1'b0}}), .in1(E), .out(shifter), .sel(select));  // open: en
  Subtractor #(.width(5)) subtractor_1 (.a(float[14:10]), .b(5'b01111), .out(E));  // open: bin, bout
  Comparator #(.width(5)) comparator_1 (.a(E), .b({5{1'b0}}), .gt(comparator_1_gt), .eq(comparator_1_eq));  // open: lt
  or or_1 (select, comparator_1_gt, comparator_1_eq);
  assign operand = {{21{1'b0}}, {1'b1, float[9:0]}};  // Bit_Extender bit_extender_1
  Shifter #(.width(32)) shifter_1 (.in(operand), .\dist (shifter), .out({mid, out}));
  Negator #(.width(32)) negator_1 (.in({{10{1'b0}}, mid}), .out(sign_mid));
  Multiplexer #(.width(32)) multiplexer_2 (.in0({32{1'b0}}), .in1(\final ), .out(\int ), .sel(select));  // open: en
  Multiplexer #(.width(32)) multiplexer_3 (
    .in0({{10{1'b0}}, mid}), .in1(sign_mid), .out(\final ), .sel(float[15]));  // open: en

  // Other names for the same wires on the sheet: exponent[4:0] = float[14:10]; sign = float[15]; out[31:10] = mid;
  //   temp_int[21:0] = mid; fraction[9:0] = float[9:0]; temp[9:0] = float[9:0]
endmodule
