// Logisim project myCPUCorrect3.circ as structural Verilog: 9 circuits, main circuit main
module main (
  input  in_1,
  output [31:0] out_2,
  output [31:0] out_3,
  output out_4,
  output [4:0] out_5,
  output [31:0] out_6,
  output out_7,
  output [31:0] out_8,
  output [31:0] out_9
);

  wire ALUSrc, clk, ExtOp, zero;
  wire [2:0] ALUOp, DMOp, MemtoReg, PCSrc, RegDst;
  wire [4:0] _15_11, _20_16, instr_split_1_out_4;
  wire [5:0] instr_split_1_out_2, instr_split_1_out_3;
  wire [15:0] instr_split_1_out_7;
  wire [25:0] immediate_26;
  wire [31:0] adder_1_out, dm_1_out_7, GPR_rs, immediate_32, multiplexer_2_out, pc;

  Clock clock_1 (.out(clk));
  PC pc_1 (
    .in_1(clk), .in_2(in_1), .in_3(PCSrc), .in_4(pc), .in_5(immediate_32), .in_6(immediate_26),
    .in_7(GPR_rs), .pc_out(pc));
  IM im_1 (.PC(pc), .Instr(out_2));
  Instr_split instr_split_1 (
    .Instr(out_2), .out_2(instr_split_1_out_2), .out_3(instr_split_1_out_3), .out_4(instr_split_1_out_4),
    .out_5(_20_16), .out_6(_15_11), .out_7(instr_split_1_out_7), .out_8(immediate_26));
  control control_1 (
    .opcode(instr_split_1_out_2), .funct(instr_split_1_out_3), .in_3(zero), .MemtoReg(MemtoReg),
    .MemWrite(out_7), .ALUOp(ALUOp), .ALUSrc(ALUSrc), .RegDst(RegDst), .RegWrite(out_4), .ExtOp(ExtOp),
    .PCSrc(PCSrc), .DMOp(DMOp));
  EXT ext_1 (.in_1(instr_split_1_out_7), .ExtOp(ExtOp), .out_3(immediate_32));
  GRF grf_1 (
    .A1(instr_split_1_out_4), .A2(_20_16), .A3(out_5), .WD(out_6), .RD1(GPR_rs), .RD2(out_9), .clk(clk),
    .reset(in_1), .WE(out_4));
  Multiplexer #(.select(3), .width(5)) multiplexer_1 (
    .in0(_20_16), .in1(_15_11), .in2({5{1'b1}}), .out(out_5), .sel(RegDst));  // open: in3, in4, in5, in6, in7, en
  Multiplexer #(.width(32)) multiplexer_2 (
    .in0(out_9), .in1(immediate_32), .out(multiplexer_2_out), .sel(ALUSrc));  // open: en
  ALU alu_1 (.SrcA(GPR_rs), .SrcB(multiplexer_2_out), .signal(ALUOp), .zero(zero), .ALUResult(out_8));
  DM dm_1 (.in_1(out_8), .in_2(out_9), .in_3(clk), .in_4(out_7), .in_5(in_1), .in_6(DMOp), .out_7(dm_1_out_7));
  Adder #(.width(32)) adder_1 (.a(pc), .b(32'h4), .out(adder_1_out));  // open: cin, cout
  Multiplexer #(.select(3), .width(32)) multiplexer_3 (
    .in0(out_8), .in1(dm_1_out_7), .in2(adder_1_out), .out(out_6), .sel(MemtoReg));  // open: in3, in4, in5, in6, in7, en
  Adder #(.width(32)) adder_2 (.a(pc), .b(32'h3000), .out(out_3));  // open: cin, cout

  // Other names for the same wires on the sheet: Instr[31:0] = out_2; MemAddr[31:0] = out_8; MemData[31:0] = out_9;
  //   MemWrite = out_7; RegAddr[4:0] = out_5; RegData[31:0] = out_6; RegWrite = out_4; reset = in_1
endmodule

module GRF (
  input  clk,
  input  reset,
  input  WE,
  input  [4:0] A1,
  input  [4:0] A2,
  input  [4:0] A3,
  input  [31:0] WD,
  output [31:0] RD1,
  output [31:0] RD2
);

  wire WE1, WE2, WE3, WE4, WE5, WE6, WE7, WE8, WE9, WE10, WE11, WE12, WE13, WE14, WE15, WE16, WE17, WE18,
       WE19, WE20, WE21, WE22, WE23, WE24, WE25, WE26, WE27, WE28, WE29, WE30, WE31, WE32;
  wire [31:0] data1, data2, data3, data4, data5, data6, data7, data8, data9, data10, data11, data12, data13,
       data14, data15, data16, data17, data18, data19, data20, data21, data22, data23, data24, data25,
       data26, data27, data28, data29, data30, data31, data32;

  Register #(.width(32)) register_1 (.D(WD), .en(WE1), .Q(data1), .clk(clk), .clr(reset));
  Register #(.width(32)) register_2 (.D(WD), .en(WE2), .Q(data2), .clk(clk), .clr(reset));
  Register #(.width(32)) register_3 (.D(WD), .en(WE3), .Q(data3), .clk(clk), .clr(reset));
  Register #(.width(32)) register_4 (.D(WD), .en(WE4), .Q(data4), .clk(clk), .clr(reset));
  Register #(.width(32)) register_5 (.D(WD), .en(WE5), .Q(data5), .clk(clk), .clr(reset));
  Register #(.width(32)) register_6 (.D(WD), .en(WE6), .Q(data6), .clk(clk), .clr(reset));
  Register #(.width(32)) register_7 (.D(WD), .en(WE7), .Q(data7), .clk(clk), .clr(reset));
  Register #(.width(32)) register_8 (.D(WD), .en(WE8), .Q(data8), .clk(clk), .clr(reset));
  Register #(.width(32)) register_9 (.D(WD), .en(WE9), .Q(data9), .clk(clk), .clr(reset));
  Register #(.width(32)) register_10 (.D(WD), .en(WE10), .Q(data10), .clk(clk), .clr(reset));
  Register #(.width(32)) register_11 (.D(WD), .en(WE11), .Q(data11), .clk(clk), .clr(reset));
  Register #(.width(32)) register_12 (.D(WD), .en(WE12), .Q(data12), .clk(clk), .clr(reset));
  Register #(.width(32)) register_13 (.D(WD), .en(WE13), .Q(data13), .clk(clk), .clr(reset));
  Register #(.width(32)) register_14 (.D(WD), .en(WE14), .Q(data14), .clk(clk), .clr(reset));
  Register #(.width(32)) register_15 (.D(WD), .en(WE15), .Q(data15), .clk(clk), .clr(reset));
  Register #(.width(32)) register_16 (.D(WD), .en(WE16), .Q(data16), .clk(clk), .clr(reset));
  Register #(.width(32)) register_17 (.D(WD), .en(WE17), .Q(data17), .clk(clk), .clr(reset));
  Register #(.width(32)) register_18 (.D(WD), .en(WE18), .Q(data18), .clk(clk), .clr(reset));
  Register #(.width(32)) register_19 (.D(WD), .en(WE19), .Q(data19), .clk(clk), .clr(reset));
  Register #(.width(32)) register_20 (.D(WD), .en(WE20), .Q(data20), .clk(clk), .clr(reset));
  Register #(.width(32)) register_21 (.D(WD), .en(WE21), .Q(data21), .clk(clk), .clr(reset));
  Register #(.width(32)) register_22 (.D(WD), .en(WE22), .Q(data22), .clk(clk), .clr(reset));
  Register #(.width(32)) register_23 (.D(WD), .en(WE23), .Q(data23), .clk(clk), .clr(reset));
  Register #(.width(32)) register_24 (.D(WD), .en(WE24), .Q(data24), .clk(clk), .clr(reset));
  Register #(.width(32)) register_25 (.D(WD), .en(WE25), .Q(data25), .clk(clk), .clr(reset));
  Register #(.width(32)) register_26 (.D(WD), .en(WE26), .Q(data26), .clk(clk), .clr(reset));
  Register #(.width(32)) register_27 (.D(WD), .en(WE27), .Q(data27), .clk(clk), .clr(reset));
  Register #(.width(32)) register_28 (.D(WD), .en(WE28), .Q(data28), .clk(clk), .clr(reset));
  Register #(.width(32)) register_29 (.D(WD), .en(WE29), .Q(data29), .clk(clk), .clr(reset));
  Register #(.width(32)) register_30 (.D(WD), .en(WE30), .Q(data30), .clk(clk), .clr(reset));
  Register #(.width(32)) register_31 (.D(WD), .en(WE31), .Q(data31), .clk(clk), .clr(reset));
  Register #(.width(32)) register_32 (.D(WD), .en(WE32), .Q(data32), .clk(clk), .clr(reset));
  Decoder #(.select(5), .disabled(0)) decoder_1 (
    .out0(WE1), .out1(WE2), .out2(WE3), .out3(WE4), .out4(WE5), .out5(WE6), .out6(WE7), .out7(WE8),
    .out8(WE9), .out9(WE10), .out10(WE11), .out11(WE12), .out12(WE13), .out13(WE14), .out14(WE15),
    .out15(WE16), .out16(WE17), .out17(WE18), .out18(WE19), .out19(WE20), .out20(WE21), .out21(WE22),
    .out22(WE23), .out23(WE24), .out24(WE25), .out25(WE26), .out26(WE27), .out27(WE28), .out28(WE29),
    .out29(WE30), .out30(WE31), .out31(WE32), .sel(A3), .en(WE));
  Multiplexer #(.select(5), .width(32)) multiplexer_1 (
    .in0({32{1'b0}}), .in1(data2), .in2(data3), .in3(data4), .in4(data5), .in5(data6), .in6(data7),
    .in7(data8), .in8(data9), .in9(data10), .in10(data11), .in11(data12), .in12(data13), .in13(data14),
    .in14(data15), .in15(data16), .in16(data17), .in17(data18), .in18(data19), .in19(data20), .in20(data21),
    .in21(data22), .in22(data23), .in23(data24), .in24(data25), .in25(data26), .in26(data27), .in27(data28),
    .in28(data29), .in29(data30), .in30(data31), .in31(data32), .out(RD1), .sel(A1));  // open: en
  Multiplexer #(.select(5), .width(32)) multiplexer_2 (
    .in0({32{1'b0}}), .in1(data2), .in2(data3), .in3(data4), .in4(data5), .in5(data6), .in6(data7),
    .in7(data8), .in8(data9), .in9(data10), .in10(data11), .in11(data12), .in12(data13), .in13(data14),
    .in14(data15), .in15(data16), .in16(data17), .in17(data18), .in18(data19), .in19(data20), .in20(data21),
    .in21(data22), .in22(data23), .in23(data24), .in24(data25), .in25(data26), .in26(data27), .in27(data28),
    .in28(data29), .in29(data30), .in30(data31), .in31(data32), .out(RD2), .sel(A2));  // open: en
endmodule

module ALU (
  input  [31:0] SrcA,
  input  [31:0] SrcB,
  input  [2:0] signal,
  output zero,
  output [31:0] ALUResult
);

  wire [31:0] add, \and , lui, \or , shifter_1_out, sub;

  assign \or  = SrcA | SrcB;  // OR_Gate or_1, 32 bits wide
  assign \and  = SrcA & SrcB;  // AND_Gate and_1, 32 bits wide
  Adder #(.width(32)) adder_1 (.a(SrcA), .b(SrcB), .out(add));  // open: cin, cout
  Subtractor #(.width(32)) subtractor_1 (.a(SrcA), .b(SrcB), .out(sub));  // open: bin, bout
  Shifter #(.width(32)) shifter_1 (.in(SrcB), .\dist (5'b10000), .out(shifter_1_out));
  assign lui = SrcA | shifter_1_out;  // OR_Gate or_2, 32 bits wide
  Comparator #(.width(32), .mode("unsigned")) comparator_1 (.a(sub), .b({32{1'b0}}), .eq(zero));  // open: gt, lt
  Multiplexer #(.select(3), .width(32)) multiplexer_1 (
    .in0(\and ), .in1(\or ), .in2(add), .in3(lui), .in6(sub), .out(ALUResult), .sel(signal));  // open: in4, in5, in7, en
endmodule

module IM (
  input  [31:0] PC,
  output [31:0] Instr
);

  ROM #(.addrWidth(12), .dataWidth(32)) rom_1 (.addr(PC[13:2]), .data(Instr));  // open: sel

  // Notes on the sheet:
  //   contents of rom_1 (hex, n*v repeats v):
  //   341c0000 341d0000 34013456 210820 8c010004 ac010004 3c027878 411822 3c051234 34040005 0 ac85ffff
  //   8c83ffff 10650001 1000000d 34670404 10e3000b 0 3c087777 3508ffff 80022 34001100 e65020 34080000
  //   34090001 340a0001 10a4020 1109fffe 1000ffff
endmodule

module PC (
  input  in_1,
  input  in_2,
  input  [2:0] in_3,
  input  [31:0] in_4,
  input  [31:0] in_5,
  input  [25:0] in_6,
  input  [31:0] in_7,
  output [31:0] pc_out
);

  wire [31:0] beq, multiplexer_1_out, pc_4, pc_4_offset_4;

  Adder #(.width(32)) adder_1 (.a(in_4), .b(32'h4), .out(pc_4));  // open: cin, cout
  Shifter #(.width(32)) shifter_1 (.in(in_5), .\dist (5'b00010), .out(beq));
  Adder #(.width(32)) adder_2 (.a(pc_4), .b(beq), .out(pc_4_offset_4));  // open: cin, cout
  Multiplexer #(.select(3), .width(32)) multiplexer_1 (
    .in0(pc_4), .in1(pc_4_offset_4), .in2({in_4[31:28], in_6, 2'b00}), .in3(in_7), .out(multiplexer_1_out),
    .sel(in_3));  // open: in4, in5, in6, in7, en
  Register #(.width(32)) PC (.D(multiplexer_1_out), .Q(pc_out), .clk(in_1), .clr(in_2));  // open: en

  // Other names for the same wires on the sheet: clk = in_1; GPR_rs[31:0] = in_7; immediate_32[31:0] = in_5;
  //   immediate_26[25:0] = in_6; pc31___28__instr__0_2[31:2] = {in_4[31:28], in_6}; pc31___28[3:0] = in_4[31:28];
  //   pc_in[31:0] = in_4; PCSrc[2:0] = in_3; reset = in_2
endmodule

module Instr_split (
  input  [31:0] Instr,
  output [5:0] out_2,
  output [5:0] out_3,
  output [4:0] out_4,
  output [4:0] out_5,
  output [4:0] out_6,
  output [15:0] out_7,
  output [25:0] out_8
);


  assign out_2 = Instr[31:26];
  assign out_3 = Instr[5:0];
  assign out_4 = Instr[25:21];
  assign out_5 = Instr[20:16];
  assign out_6 = Instr[15:11];
  assign out_7 = Instr[15:0];
  assign out_8 = Instr[25:0];

  // Other names for the same wires on the sheet: _20_16[4:0] = Instr[20:16]; _25_0[25:0] = Instr[25:0];
  //   _25_21[4:0] = Instr[25:21]; funct[5:0] = Instr[5:0]; immediate[15:0] = Instr[15:0]; _15_11[4:0] = Instr[15:11];
  //   opcode[5:0] = Instr[31:26]
endmodule

module EXT (
  input  [15:0] in_1,
  input  ExtOp,
  output [31:0] out_3
);

  wire [31:0] bit_extender_1_out, bit_extender_2_out;

  assign bit_extender_1_out = {{16{1'b0}}, in_1};  // Bit_Extender bit_extender_1
  assign bit_extender_2_out = {{16{in_1[15]}}, in_1};  // Bit_Extender bit_extender_2
  Multiplexer #(.width(32)) multiplexer_1 (
    .in0(bit_extender_1_out), .in1(bit_extender_2_out), .out(out_3), .sel(ExtOp));  // open: en

  // Other names for the same wires on the sheet: imm[15:0] = in_1
endmodule

module control (
  input  [5:0] opcode,
  input  [5:0] funct,
  input  in_3,
  output [2:0] MemtoReg,
  output MemWrite,
  output [2:0] ALUOp,
  output ALUSrc,
  output [2:0] RegDst,
  output RegWrite,
  output ExtOp,
  output [2:0] PCSrc,
  output [2:0] DMOp
);

  wire _15_11, add, add_check, \and , and_check, beq, beq_jump, Branch, \byte , halfword, j, jal, jr,
       jr_check, lb, lh, lui, lw, not_1_out, not_2_out, not_3_out, not_4_out, not_5_out, not_6_out,
       not_7_out, not_8_out, not_9_out, not_10_out, not_11_out, not_12_out, or_15_out, ori, R, sb, sh, sub,
       sub_check, sw, to_add, to_and, to_lui, to_or, to_sub, word;

  not not_1 (not_1_out, opcode[5]);
  not not_2 (not_2_out, opcode[3]);
  not not_3 (not_3_out, opcode[4]);
  not not_4 (not_4_out, opcode[2]);
  not not_5 (not_5_out, opcode[1]);
  not not_6 (not_6_out, opcode[0]);
  and u_ori (ori, not_1_out, not_3_out, opcode[3], opcode[2], not_5_out, opcode[0]);
  and u_lw (lw, opcode[5], not_3_out, not_2_out, not_4_out, opcode[1], opcode[0]);
  and u_sw (sw, opcode[5], not_3_out, opcode[3], not_4_out, opcode[1], opcode[0]);
  and u_beq (beq, not_1_out, not_3_out, not_2_out, opcode[2], not_5_out, not_6_out);
  and u_R (R, not_1_out, not_3_out, not_2_out, not_4_out, not_5_out, not_6_out);
  and u_lui (lui, not_1_out, not_3_out, opcode[3], opcode[2], opcode[1], opcode[0]);
  and u_j (j, not_1_out, not_3_out, not_2_out, not_4_out, opcode[1], not_6_out);
  and u_lb (lb, opcode[5], not_3_out, not_2_out, not_4_out, not_5_out, not_6_out);
  and u_sb (sb, opcode[5], not_3_out, opcode[3], not_4_out, not_5_out, not_6_out);
  and u_lh (lh, opcode[5], not_3_out, not_2_out, not_4_out, not_5_out, opcode[0]);
  and u_sh (sh, opcode[5], not_3_out, opcode[3], not_4_out, not_5_out, opcode[0]);
  and u_jal (jal, not_1_out, not_3_out, not_2_out, not_4_out, opcode[1], opcode[0]);
  not not_7 (not_7_out, funct[5]);
  not not_8 (not_8_out, funct[3]);
  not not_9 (not_9_out, funct[4]);
  not not_10 (not_10_out, funct[2]);
  not not_11 (not_11_out, funct[1]);
  not not_12 (not_12_out, funct[0]);
  and u_add_check (add_check, funct[5], not_9_out, not_8_out, not_10_out, not_11_out, not_12_out);
  and u_sub_check (sub_check, funct[5], not_9_out, not_8_out, not_10_out, funct[1], not_12_out);
  and u_and_check (and_check, funct[5], not_9_out, not_8_out, funct[2], not_11_out, not_12_out);
  and u_jr_check (jr_check, not_7_out, not_9_out, funct[3], not_10_out, not_11_out, not_12_out);
  or or_1 (word, lw, sw);
  or or_2 (\byte , lb, sb);
  or or_3 (halfword, lh, sh);
  and u_add (add, add_check, R);
  and u_sub (sub, sub_check, R);
  and u_and (\and , and_check, R);
  and u_jr (jr, jr_check, R);
  or or_4 (MemWrite, sw, sh, sb);
  buf or_5 (Branch, beq);  // OR_Gate
  or or_6 (to_add, word, add, \byte , halfword);
  or or_7 (to_sub, sub, beq);
  buf or_8 (to_or, ori);  // OR_Gate
  buf or_9 (to_and, \and );  // OR_Gate
  buf or_10 (to_lui, lui);  // OR_Gate
  or or_11 (ALUSrc, word, ori, lui, \byte , halfword);
  or or_12 (_15_11, add, \and , sub);
  or or_13 (RegWrite, jal, lb, add, sub, ori, lw, lui, \and );
  or or_14 (ExtOp, word, beq, \byte , halfword);
  Priority_Encoder priority_encoder_1 (
    .in0(1'b1), .in1(word), .in2(halfword), .in3(\byte ), .out(DMOp));  // open: in4, in5, in6, in7, en_in, gs, en_out
  or or_15 (or_15_out, lw, lh, lb);
  Priority_Encoder priority_encoder_2 (
    .in0(1'b1), .in1(or_15_out), .in2(jal), .out(MemtoReg));  // open: in3, in4, in5, in6, in7, en_in, gs, en_out
  and and_2 (beq_jump, Branch, in_3);
  Priority_Encoder priority_encoder_3 (
    .in0(1'b1), .in1(_15_11), .in2(jal), .out(RegDst));  // open: in3, in4, in5, in6, in7, en_in, gs, en_out
  Priority_Encoder priority_encoder_4 (
    .in0(to_and), .in1(to_or), .in2(to_add), .in3(to_lui), .in6(to_sub), .out(ALUOp));  // open: in4, in5, in7, en_in, gs, en_out
  Priority_Encoder priority_encoder_5 (
    .in0(1'b1), .in1(beq_jump), .in2(jal), .in3(jr), .out(PCSrc));  // open: in4, in5, in6, in7, en_in, gs, en_out

  // Other names for the same wires on the sheet: zero = in_3
endmodule

module DM (
  input  [31:0] in_1,
  input  [31:0] in_2,
  input  in_3,
  input  in_4,
  input  in_5,
  input  [2:0] in_6,
  output [31:0] out_7
);

  wire [7:0] multiplexer_1_out;
  wire [15:0] multiplexer_2_out;
  wire [31:0] bit_extender_1_out, bit_extender_2_out, factwrite, memword, multiplexer_3_out,
       multiplexer_4_out;

  Multiplexer #(.select(2), .width(8)) multiplexer_1 (
    .in0(memword[7:0]), .in1(memword[15:8]), .in2(memword[23:16]), .in3(memword[31:24]),
    .out(multiplexer_1_out), .sel(in_1[1:0]));  // open: en
  Multiplexer #(.width(16)) multiplexer_2 (
    .in0(memword[15:0]), .in1(memword[31:16]), .out(multiplexer_2_out), .sel(in_1[1]));  // open: en
  assign bit_extender_1_out = {{16{multiplexer_2_out[15]}}, multiplexer_2_out};  // Bit_Extender bit_extender_1
  assign bit_extender_2_out = {{24{multiplexer_1_out[7]}}, multiplexer_1_out};  // Bit_Extender bit_extender_2
  Multiplexer #(.width(32)) multiplexer_3 (
    .in0({memword[31:16], in_2[15:0]}), .in1({in_2[15:0], memword[15:0]}), .out(multiplexer_3_out),
    .sel(in_1[1]));  // open: en
  Multiplexer #(.select(2), .width(32)) multiplexer_4 (
    .in0({memword[31:8], in_2[7:0]}), .in1({memword[31:16], in_2[7:0], memword[7:0]}),
    .in2({memword[31:24], in_2[7:0], memword[15:0]}), .in3({in_2[7:0], memword[23:0]}),
    .out(multiplexer_4_out), .sel(in_1[1:0]));  // open: en
  Multiplexer #(.select(3), .width(32)) multiplexer_5 (
    .in0({32{1'b0}}), .in1(memword), .in2(bit_extender_1_out), .in3(bit_extender_2_out), .out(out_7),
    .sel(in_6));  // open: in4, in5, in6, in7, en
  Multiplexer #(.select(3), .width(32)) multiplexer_6 (
    .in0({32{1'b0}}), .in1(in_2), .in2(multiplexer_3_out), .in3(multiplexer_4_out), .out(factwrite),
    .sel(in_6));  // open: in4, in5, in6, in7, en
  RAM #(.addrWidth(12), .dataWidth(32), .bus("separate")) ram_1 (
    .addr(in_1[11:0]), .din(factwrite), .data(memword), .str(in_4), .clk(in_3), .clr(in_5));  // open: sel, ld

  // Other names for the same wires on the sheet: writedata[31:0] = in_2; writedata15___8[7:0] = in_2[15:8];
  //   writedata7___0[7:0] = in_2[7:0]; address[31:0] = in_1; address1___0[1:0] = in_1[1:0]; address1 = in_1[1];
  //   clk = in_3; DMOp[2:0] = in_6; memword7___0[7:0] = memword[7:0]; memword15___8[7:0] = memword[15:8];
  //   memword23___16[7:0] = memword[23:16]; memword31___24[7:0] = memword[31:24]; readdata[31:0] = out_7;
  //   reset = in_5; WE = in_4; writedata23___16[7:0] = in_2[23:16]; writedata31___24[7:0] = in_2[31:24]
endmodule
