// Logisim project 4bit_sort.circ as structural Verilog: 4 circuits, main circuit 4bit_sort
module _4bit_sort (
  input  [3:0] A,
  input  [3:0] B,
  input  [3:0] C,
  input  [3:0] D,
  output [3:0] _1,
  output [3:0] _2,
  output [3:0] _3,
  output [3:0] _4
);

  wire [3:0] compare_1_out_3, compare_1_out_4, compare_2_out_3, compare_2_out_4, compare_3_out_3,
       compare_4_out_3, compare_4_out_4, compare_6_out_3;

  compare compare_1 (.in_1(A), .in_2(B), .out_3(compare_1_out_3), .out_4(compare_1_out_4));
  compare compare_2 (.in_1(compare_1_out_4), .in_2(C), .out_3(compare_2_out_3), .out_4(compare_2_out_4));
  compare compare_3 (.in_1(compare_2_out_4), .in_2(D), .out_3(compare_3_out_3), .out_4(_4));
  compare compare_4 (.in_1(compare_1_out_3), .in_2(compare_2_out_3), .out_3(compare_4_out_3), .out_4(compare_4_out_4));
  compare compare_5 (.in_1(compare_4_out_3), .in_2(compare_6_out_3), .out_3(_1), .out_4(_2));
  compare compare_6 (.in_1(compare_4_out_4), .in_2(compare_3_out_3), .out_3(compare_6_out_3), .out_4(_3));
endmodule

module _1bit_swap (
  input  in_1,
  input  in_2,
  input  in_3,
  output out_4,
  output out_5
);

  wire and_1_out, and_2_out, and_3_out, and_4_out, not_1_out;

  not not_1 (not_1_out, in_3);
  and and_1 (and_1_out, in_1, not_1_out);
  and and_2 (and_2_out, in_2, in_3);
  and and_3 (and_3_out, in_1, in_3);
  and and_4 (and_4_out, in_2, not_1_out);
  or or_1 (out_4, and_1_out, and_2_out);
  or or_2 (out_5, and_3_out, and_4_out);
endmodule

module _4bit_swap (
  input  [3:0] I1,
  input  [3:0] I2,
  input  enable,
  output [3:0] O1,
  output [3:0] O2
);

  _1bit_swap u_1bit_swap_1 (.in_1(I1[0]), .in_2(I2[0]), .in_3(enable), .out_4(O1[0]), .out_5(O2[0]));
  _1bit_swap u_1bit_swap_2 (.in_1(I1[1]), .in_2(I2[1]), .in_3(enable), .out_4(O1[1]), .out_5(O2[1]));
  _1bit_swap u_1bit_swap_3 (.in_1(I1[2]), .in_2(I2[2]), .in_3(enable), .out_4(O1[2]), .out_5(O2[2]));
  _1bit_swap u_1bit_swap_4 (.in_1(I1[3]), .in_2(I2[3]), .in_3(enable), .out_4(O1[3]), .out_5(O2[3]));

  // Other names for the same wires on the sheet: I1_0 = I1[0]; I1_1 = I1[1]; I1_2 = I1[2]; I1_3 = I1[3]; I2_0 = I2[0];
  //   I2_1 = I2[1]; I2_2 = I2[2]; I2_3 = I2[3]; O1_0 = O1[0]; O1_1 = O1[1]; O1_2 = O1[2]; O1_3 = O1[3]; O2_0 = O2[0];
  //   O2_1 = O2[1]; O2_2 = O2[2]; O2_3 = O2[3]
endmodule

module compare (
  input  [3:0] in_1,
  input  [3:0] in_2,
  output [3:0] out_3,
  output [3:0] out_4
);

  wire comparator_1_gt;

  Comparator #(.width(4), .mode("unsigned")) comparator_1 (.a(in_1), .b(in_2), .gt(comparator_1_gt));  // open: eq, lt
  _4bit_swap u_4bit_swap_1 (.I1(in_1), .I2(in_2), .enable(comparator_1_gt), .O1(out_3), .O2(out_4));
endmodule
