// Logisim project fibonacci_1.circ as structural Verilog: 3 circuits, main circuit main
module main (
  input  [2:0] N,
  output [3:0] Nth
);

  wire signal;
  wire [3:0] calculate_1_out_2;

  print cnt (.N(N), .out_2(signal));
  calculate calculate_1 (.in_1(signal), .out_2(calculate_1_out_2));
  Multiplexer #(.width(4)) multiplexer_1 (.in0(4'b0000), .in1(calculate_1_out_2), .out(Nth), .sel(signal));  // open: en

  // Other names for the same wires on the sheet: input[2:0] = N
endmodule

module print (
  input  [2:0] N,
  output out_2
);

  wire clk_out;
  wire [3:0] bit_extender_1_out, i;

  assign bit_extender_1_out = {{1{1'b0}}, N};  // Bit_Extender bit_extender_1
  Comparator #(.width(4), .mode("unsigned")) comparator_1 (.a(i), .b(bit_extender_1_out), .gt(out_2));  // open: eq, lt
  Clock clk (.out(clk_out));
  Counter #(.width(4), .max('h8), .ongoal("stay")) counter_1 (
    .Q(i), .clk(clk_out));  // open: load, D, count, carry, clr
endmodule

module calculate (
  input  in_1,
  output [3:0] out_2
);

  wire clk, enable, selecter;
  wire [3:0] adder_1_out, multiplexer_1_out, prev;

  Clock clock_1 (.out(clk));
  Counter #(.width(1), .max('h1), .ongoal("stay")) counter_1 (
    .Q(selecter), .clk(clk));  // open: load, D, count, carry, clr
  not not_1 (enable, in_1);
  Multiplexer #(.width(4)) multiplexer_1 (
    .in0(4'b0001), .in1(out_2), .out(multiplexer_1_out), .sel(selecter));  // open: en
  Adder #(.width(4)) adder_1 (.a(prev), .b(out_2), .out(adder_1_out));  // open: cin, cout
  Register #(.width(4)) u_prev (.D(multiplexer_1_out), .en(enable), .Q(prev), .clk(clk));  // open: clr
  Register #(.width(4)) now (.D(adder_1_out), .en(enable), .Q(out_2), .clk(clk));  // open: clr

  // Other names for the same wires on the sheet: now[3:0] = out_2
endmodule
